# Fritzing sketch weatherlogger (saved by Fritzing 0.9.3b)
breadboards: 1

parts:
  Part1 = Arduino Nano (Rev3.0)
  DHT1 = DHT11 Humitidy and Temperature Sensor
  R1 = Photocell (LDR) [package=THT]
  R2 = Resistor [tolerance=±5% resistance=10k package="1206 [SMD]"]
  Part3 = Real Time Clock Module - DS1307 RTC Breakout Board
  microSD1 = MicroSD Card Module
  Part4 = Barometric Pressure Sensor - BMP180 Breakout (GY-68)
  Part5 = Breadboard Power Supply Board SMD
  VCC1 = Battery block 9V
  U1 = HALL-EFFECT [package=sc70]

nets:
  GND: Part1.GND, R2.Pin_0, Part3.GND, Part4.GND
  N1: Part1.D3, DHT1.DATA
  N2: Part1.D4, microSD1.CS
  N3: Part1.D9, U1.OUT
  N4: Part1.D11/MOSI, microSD1.MISO
  N5: Part1.D12/MISO, microSD1.MOSI
  5V: Part1.5V, R1.pin_0, Part3.5V, microSD1.VCC, U1.VCC
  N6: Part1.A5, Part3.SCL
  N7: Part1.A4, Part3.SDA, Part4.SDA
  N8: Part1.A0, R1.pin_1, R2.Pin_1
  3V3: Part1.3V3, DHT1.VDD, Part4.VCC
  N9: Part1.D13/SCK, microSD1.SCK
  GND_2: DHT1.GND, microSD1.GND, U1.GND
  N10: Part5.VIN, VCC1.+
  N11: Part5.GND, VCC1.-

custom parts:
  DHT11 Humitidy and Temperature Sensor: DHT11 Humidity and Temperature Sensor
